# Fritzing sketch ble_dimmer (saved by Fritzing 0.9.2b)
perfboards: 1

parts:
  U1 = RELAY-SOLIDSTATE [package=relay-s108t02]
  U2 = RELAY-SOLIDSTATE [package=relay-s108t02]
  U3 = RELAY-SOLIDSTATE [package=relay-s108t02]
  Power_plug1 = Power plug
  Part1 = Arduino Pro Mini v13
  LED1 = LEDs [package=led10mm]
  LED2 = LEDs [package=led10mm]
  LED3 = LEDs [package=led10mm]
  J1 = Power Jack [package=power_jack_pth_lock]
  Part4 = Bluetooth Mate Silver
  J2 = Screw terminal - 2 pins [package=THT]
  J3 = Screw terminal - 2 pins [package=THT]
  U4 = Optocoupler [package=THT]
  U5 = MOC3031-M [package=dil06]
  D1 = Schottky Diode [part_number=1N5817 package="300 mil [THT]"]  # not connected
  U6 = DIODE-ZENER [package=diode-zener]
  R1 = Resistor [tolerance=±5% resistance=220 package=THT]
  Q1 = Basic FET P-Channel [package="DPak [SMD]"]
  U7 = DIODE-ZENER [package=diode-zener]
  U8 = DIODE-ZENER [package=diode-zener]
  U9 = DIODE-ZENER [package=diode-zener]
  R2 = Resistor [tolerance=±5% resistance=220 package=THT]
  R3 = Resistor [tolerance=±5% resistance=220 package=THT]
  R4 = Resistor [tolerance=±5% resistance=220 package=THT]
  R5 = Resistor [tolerance=±5% resistance=220 package=THT]  # not connected

nets:
  N1: U1.T1, U2.T1, U3.T1, J1.GND
  N2: U1.T2, LED1.C
  N3: U1.+, Part1.D9_PWM
  GND: U1.-, Power_plug1.GND, Part1.GND, Part4.GND
  N4: U2.T2, LED2.C
  N5: U2.+, Part1.D4
  N6: U2.-, U3.-
  N7: U3.T2, LED3.C
  N8: U3.+, Part1.D2
  N9: Power_plug1.VCC, Part1.RAW
  VCC: Part1.VCC, Part4.VCC
  N10: Part1.D11_PWM/MOSI, Part4.TX_5V
  N11: Part1.D10_PWM/SS, Part4.RX_5V
  N12: LED1.A, LED2.A, LED3.A, J1.GNDBREAK
  N13: J2.pin1, R1.Pin_0, Q1.drain, R3.Pin_0
  N14: J2.pin2, R2.Pin_0
  N15: J3.pin1, Q1.source
  N16: U4.Pin_1, U6.A, U9.A
  N17: U4.Pin_2, U7.C
  N18: U4.Pin_5, R4.Pin_0
  N19: U5.4, Q1.Gate
  N20: U5.6, R3.Pin_1
  N21: U6.C, R1.Pin_1, U7.A
  N22: U8.A, U9.C, R2.Pin_1
